// Digital circuit RISCV_Top.dig as structural Verilog
module RISCV_Top (
  input  clk,
  input  rst,
  output [31:0] out_3,
  output [7:0] out_4,
  output [2:0] funct3,
  output [31:0] instr,
  output [6:0] funct7,
  output [6:0] opcode,
  output [4:0] rd,
  output [4:0] rs1,
  output [4:0] rs2,
  output [1:0] ALUOp,
  output [3:0] ALUControl,
  output [31:0] WriteData,
  output [31:0] RD1,
  output [31:0] RD2,
  output [31:0] imm,
  output [31:0] pc
);

  wire ALUSrc, and_3_out, and_4_out, and_5_out, and_6_out, and_7_out, and_8_out, AUIPC, Branch, clk_t,
       comparator_1_eq, comparator_2_eq, D_out, Debug_Mode_out, decoder_1_out_0, decoder_1_out_1,
       decoder_1_out_4, decoder_1_out_5, decoder_1_out_6, decoder_1_out_7, I, Jal, Jalr, LUI, MemRead,
       MemtoReg, MemWrite, not_1_out, not_2_out, not_3_out, or_2_out, P1, P2, P3, P4, P5, P6, R, RegWrite,
       regWrite_t, takeBranch, write_jal, Zero;
  wire [6:0] modified_funct7;
  wire [6:6] graphiccard_1_d;
  wire [15:0] D1, D2, D3, D4, D5, D6;
  wire [31:0] ALU_in2, Jalr_Adder_s, multiplexer_1_out, multiplexer_3_out, multiplexer_8_out,
       multiplexer_9_out, PC_branch, PC_jalr_target, PC_next, PC_plus4, ReadData, Result, WriteData_from_mem;

  D_FF_AS #(.Bits(32)) Program_Counter (.Set(1'b0), .D(PC_next), .C(clk_t), .Clr(rst), .Q(out_3));  // open: nQ
  Multiplexer #(.Bits(32)) multiplexer_1 (.sel(takeBranch), .in_0(PC_plus4), .in_1(PC_branch), .out(multiplexer_1_out));
  Button D (.out(D_out));
  DipSwitch #(.dipDefault("true")) Debug_Mode (.out(Debug_Mode_out));
  Comparator #(.Bits(5)) comparator_1 (.a(instr[11:7]), .b({5{1'b0}}), .eq(comparator_1_eq));  // open: gt, lt
  Multiplexer multiplexer_2 (.sel(Debug_Mode_out), .in_0(clk), .in_1(D_out), .out(clk_t));
  LED led_1 (.in(Debug_Mode_out));
  or or_1 (write_jal, Jal, Jalr);
  not not_1 (not_1_out, comparator_1_eq);
  Multiplexer #(.Bits(32)) multiplexer_3 (
    .sel(Jal), .in_0(multiplexer_1_out), .in_1(PC_branch), .out(multiplexer_3_out));
  and and_1 (regWrite_t, RegWrite, not_1_out);
  SixteenSeg sixteenseg_1 (.led(D1), .dp(P1));
  SixteenSeg sixteenseg_2 (.led(D2), .dp(P2));
  Multiplexer #(.Bits(32)) multiplexer_4 (.sel(Jalr), .in_0(multiplexer_3_out), .in_1(PC_jalr_target), .out(PC_next));
  SixteenSeg sixteenseg_3 (.led(D3), .dp(P3));
  SixteenSeg sixteenseg_4 (.led(D4), .dp(P4));
  Add #(.Bits(32)) PC_Adder (.a(out_3), .b(32'h4), .c_i(1'b0), .s(PC_plus4));  // open: c_o
  Add #(.Bits(32)) Branch_Adder (.a(out_3), .b(imm), .c_i(1'b0), .s(PC_branch));  // open: c_o
  ROM #(.AddrBits(8), .Bits(32)) Instruction_Memory (
    .A(out_3[9:2]), .sel(1'b1), .D({funct7, instr[24:15], funct3, instr[11:0]}));
  SixteenSeg sixteenseg_5 (.led(D5), .dp(P5));
  SixteenSeg sixteenseg_6 (.led(D6), .dp(P6));
  Add #(.Bits(32)) Jalr_Adder (.a(RD1), .b(imm), .c_i(1'b0), .s(Jalr_Adder_s));  // open: c_o
  signExtend Sign_Extend (.instr({funct7, instr[24:15], funct3, instr[11:0]}), .opcode(instr[6:0]), .imm(imm));
  assign PC_jalr_target = Jalr_Adder_s & 32'hfffffffe;  // And and_2, 32 bits wide
  controlUnit Control_Unit (
    .opcode(instr[6:0]), .Branch(Branch), .MemRead(MemRead), .MemtoReg(MemtoReg), .ALUOp(ALUOp),
    .MemWrite(MemWrite), .ALUSrc(ALUSrc), .RegWrite(RegWrite), .Jal(Jal), .Jalr(Jalr), .LUI(LUI),
    .AUIPC(AUIPC), .I(I), .R(R));
  Comparator #(.Bits(3)) comparator_2 (.a(funct3), .b(3'b101), .eq(comparator_2_eq));  // open: gt, lt
  RegisterFile #(.AddrBits(5), .Bits(32)) Register_File (
    .Din(WriteData), .we(regWrite_t), .Rw(instr[11:7]), .C(clk_t), .Ra(instr[19:15]), .Rb(instr[24:20]),
    .Da(RD1), .Db(RD2));
  Decoder #(.Selector_Bits(3)) decoder_1 (
    .sel(funct3), .out_0(decoder_1_out_0), .out_1(decoder_1_out_1), .out_4(decoder_1_out_4),
    .out_5(decoder_1_out_5), .out_6(decoder_1_out_6), .out_7(decoder_1_out_7));  // open: out_2, out_3
  Multiplexer #(.Bits(32)) multiplexer_5 (.sel(ALUSrc), .in_0(RD2), .in_1(imm), .out(ALU_in2));
  not not_2 (not_2_out, Zero);
  Multiplexer #(.Bits(7)) multiplexer_6 (.sel(comparator_2_eq), .in_0({7{1'b0}}), .in_1(funct7), .out(modified_funct7));
  not not_3 (not_3_out, Result[0]);
  GraphicCard #(.graphicHeight(128), .graphicWidth(128), .Bits(7)) graphiccard_1 (
    .A(Result[14:0]), .str(MemWrite), .C(clk_t), .ld(1'b0), .B(1'b0), .D({graphiccard_1_d[6], RD2[5:0]}));
  and and_3 (and_3_out, decoder_1_out_0, Zero);
  and and_4 (and_4_out, decoder_1_out_1, not_2_out);
  and and_5 (and_5_out, decoder_1_out_4, Result[0]);
  and and_6 (and_6_out, decoder_1_out_5, not_3_out);
  and and_7 (and_7_out, decoder_1_out_6, Result[0]);
  and and_8 (and_8_out, not_3_out, decoder_1_out_7);
  aluControl ALU_Control (.funct3(funct3), .funct7(modified_funct7), .ALUOp(ALUOp), .ALUControl(ALUControl));
  alu ALU (.A(RD1), .B(ALU_in2), .ALUControl(ALUControl), .Zero(Zero), .Result(Result));
  // Probe on {graphiccard_1_d[6], RD2[5:0]}
  RAMDualPort #(.AddrBits(12), .Bits(32)) Data_Memory (
    .A(Result[13:2]), .Din(RD2), .str(MemWrite), .C(clk_t), .ld(MemRead), .D(ReadData));
  or or_2 (or_2_out, and_3_out, and_4_out, and_5_out, and_6_out, and_7_out, and_8_out);
  Multiplexer #(.Bits(32)) multiplexer_7 (.sel(MemtoReg), .in_0(Result), .in_1(ReadData), .out(WriteData_from_mem));
  and and_9 (takeBranch, Branch, or_2_out);
  Multiplexer #(.Bits(32)) multiplexer_8 (
    .sel(write_jal), .in_0(WriteData_from_mem), .in_1(PC_plus4), .out(multiplexer_8_out));
  testDisplay testdisplay_1 (
    .D1(D1), .P1(P1), .D2(D2), .P2(P2), .D3(D3), .P3(P3), .D4(D4), .P4(P4), .D5(D5), .P5(P5), .D6(D6),
    .P6(P6), .opcode(instr[6:0]), .ALUControl(ALUControl), .funct3(funct3), .funct7(funct7));
  Multiplexer #(.Bits(32)) multiplexer_9 (
    .sel(AUIPC), .in_0(multiplexer_8_out), .in_1(PC_branch), .out(multiplexer_9_out));
  Multiplexer #(.Bits(32)) multiplexer_10 (.sel(LUI), .in_0(multiplexer_9_out), .in_1(imm), .out(WriteData));

  assign {instr[31:25], instr[14:12]} = {funct7, funct3};
  assign opcode = instr[6:0];
  assign out_4 = out_3[9:2];
  assign pc = out_3;
  assign rd = instr[11:7];
  assign rs1 = instr[19:15];
  assign rs2 = instr[24:20];
  // also tied to GND on the sheet: graphiccard_1_d[6]

  // Other names for the same wires on the sheet: slt_result = Result[0]; PC_jal_target[31:0] = PC_branch;
  //   WriteData_from_auipc[31:0] = PC_branch; WriteData_from_jal[31:0] = PC_plus4; WriteData_from_lui[31:0] = imm

  // Notes on the sheet:
  //   clk: Hz: 5
  //   RISCV PROCESSOR
  //   DEBUGGING SECTION
  //   INSTRUCTION DISPLAY
  //   contents of Instruction_Memory (hex, n*v repeats v):
  //   93,213,100113,8000193,93,20a023,108093,fe309ce3,120213,fe3216e3
  //   ,500113,4202023,2202023,20202623
  //   opcode
  //   funct3
  //   funct7
  //   rs1
  //   rs2
  //   rd
  //   Graphics
endmodule

/* Code that sets the parameters or builds the circuit:
addi x1, x0, 5
addi x2, x0, 4
LOOP:
    add x3, x1, x3
    addi x2, x2, -1
    bne x2, x0, LOOP
*/
