// Digital circuit testDisplay.dig as structural Verilog
module testDisplay (
  input  [6:0] opcode,
  input  [3:0] ALUControl,
  input  [2:0] funct3,
  output [15:0] D1,
  output P1,
  output P2,
  output P3,
  output P4,
  output P5,
  output P6,
  output [15:0] D2,
  output [15:0] D3,
  output [15:0] D4,
  output [15:0] D5,
  output [15:0] D6
);

  wire B, I, JAL, JALR, L, not_1_out, not_2_out, not_3_out, not_4_out, not_5_out, not_6_out, not_7_out, R, S;
  wire [2:0] or_1_out;
  wire [6:0] multiplexer_1_out, multiplexer_2_out, multiplexer_3_out, multiplexer_4_out, multiplexer_5_out,
       multiplexer_6_out, multiplexer_7_out, multiplexer_8_out, multiplexer_9_out, multiplexer_10_out,
       multiplexer_11_out, multiplexer_12_out, multiplexer_13_out, multiplexer_14_out, multiplexer_15_out,
       multiplexer_16_out;

  not not_1 (not_1_out, opcode[6]);
  not not_2 (not_2_out, opcode[5]);
  not not_3 (not_3_out, opcode[4]);
  not not_4 (not_4_out, opcode[3]);
  not not_5 (not_5_out, opcode[2]);
  not not_6 (not_6_out, opcode[1]);
  not not_7 (not_7_out, opcode[0]);
  and and_1 (L, opcode[0], opcode[1], not_5_out, not_4_out, not_3_out, not_2_out, not_1_out);
  and and_2 (S, opcode[0], opcode[1], not_5_out, not_4_out, not_3_out, opcode[5], not_1_out);
  and and_3 (B, opcode[0], opcode[1], not_5_out, not_4_out, not_3_out, opcode[5], opcode[6]);
  and and_4 (I, opcode[0], opcode[1], not_5_out, not_4_out, opcode[4], not_2_out, not_1_out);
  and and_5 (R, opcode[0], opcode[1], not_5_out, not_4_out, opcode[4], opcode[5], not_1_out);
  and and_6 (JAL, opcode[0], opcode[1], opcode[2], opcode[3], not_3_out, opcode[5], opcode[6]);
  and and_7 (JALR, opcode[0], opcode[1], opcode[2], not_4_out, not_3_out, opcode[5], opcode[6]);
  or or_1 (or_1_out[2], I, B, S, L);
  or or_2 (or_1_out[1], JAL, R, S, L);
  or or_3 (or_1_out[0], JALR, R, B, L);
  Multiplexer #(.Selector_Bits(3), .Bits(7)) multiplexer_1 (
    .sel(ALUControl[2:0]), .in_0(7'b1000001), .in_1(7'b0100000), .in_2(7'b1000001), .in_3(7'b0100000),
    .in_4(7'b0100000), .in_5(7'b0100000), .in_6(7'b1010011), .in_7(7'b1010011), .out(multiplexer_1_out));
  Multiplexer #(.Selector_Bits(3), .Bits(7)) multiplexer_2 (
    .sel(ALUControl[2:0]), .in_0(7'b1001110), .in_1(7'b1001111), .in_2(7'b1000100), .in_3(7'b0100000),
    .in_4(7'b0100000), .in_5(7'b0100000), .in_6(7'b1010101), .in_7(7'b1001100), .out(multiplexer_2_out));
  Multiplexer #(.Selector_Bits(3), .Bits(7)) multiplexer_3 (
    .sel(ALUControl[2:0]), .in_0(7'b1000100), .in_1(7'b1010010), .in_2(7'b1000100), .in_3(7'b0100000),
    .in_4(7'b0100000), .in_5(7'b0100000), .in_6(7'b1000010), .in_7(7'b1010100), .out(multiplexer_3_out));
  Multiplexer #(.Selector_Bits(3), .Bits(7)) multiplexer_4 (
    .sel(or_1_out), .in_0(7'b0100000), .in_1(7'b0100000), .in_2(7'b0100000), .in_3(7'b0100000),
    .in_4(7'b0100000), .in_5(7'b0100000), .in_6(7'b0100000), .in_7(7'b0100000), .out(multiplexer_4_out));
  Multiplexer #(.Selector_Bits(3), .Bits(7)) multiplexer_5 (
    .sel(funct3), .in_0(7'b1000010), .in_1(7'b1000010), .in_2(7'b1000001), .in_3(7'b0100000),
    .in_4(7'b1000010), .in_5(7'b1000010), .in_6(7'b0100000), .in_7(7'b0100000), .out(multiplexer_5_out));
  ROM #(.AddrBits(7), .Bits(16)) ASCII (.A(multiplexer_4_out), .sel(1'b1), .D(D1));
  Multiplexer #(.Selector_Bits(3), .Bits(7)) multiplexer_6 (
    .sel(ALUControl[2:0]), .in_0(7'b1001001), .in_1(7'b1001001), .in_2(7'b1001001), .in_3(7'b0100000),
    .in_4(7'b0100000), .in_5(7'b0100000), .in_6(7'b1000010), .in_7(7'b1010100), .out(multiplexer_6_out));
  Multiplexer #(.Selector_Bits(3), .Bits(7)) multiplexer_7 (
    .sel(or_1_out), .in_0(7'b0100000), .in_1(7'b0100000), .in_2(7'b0100000), .in_3(7'b0100000),
    .in_4(7'b0100000), .in_5(7'b0100000), .in_6(7'b0100000), .in_7(7'b0100000), .out(multiplexer_7_out));
  Multiplexer #(.Selector_Bits(3), .Bits(7)) multiplexer_8 (
    .sel(funct3), .in_0(7'b1000101), .in_1(7'b1001110), .in_2(7'b1000100), .in_3(7'b0100000),
    .in_4(7'b1001100), .in_5(7'b1000111), .in_6(7'b0100000), .in_7(7'b0100000), .out(multiplexer_8_out));
  ROM #(.AddrBits(7), .Bits(16)) ASCII_2 (.A(multiplexer_7_out), .sel(1'b1), .D(D2));
  Multiplexer #(.Selector_Bits(3), .Bits(7)) multiplexer_9 (
    .sel(funct3), .in_0(7'b1010001), .in_1(7'b1000101), .in_2(7'b1000100), .in_3(7'b0100000),
    .in_4(7'b1010100), .in_5(7'b1010100), .in_6(7'b0100000), .in_7(7'b0100000), .out(multiplexer_9_out));
  Multiplexer #(.Selector_Bits(3), .Bits(7)) multiplexer_10 (
    .sel(or_1_out), .in_0(7'b0100000), .in_1(7'b1001010), .in_2(7'b0100000), .in_3(7'b0100000),
    .in_4(multiplexer_1_out), .in_5(7'b0100000), .in_6(7'b0100000), .in_7(7'b0100000),
    .out(multiplexer_10_out));
  ROM #(.AddrBits(7), .Bits(16)) ASCII_3 (.A(multiplexer_10_out), .sel(1'b1), .D(D3));
  Multiplexer #(.Selector_Bits(3), .Bits(7)) multiplexer_11 (
    .sel(ALUControl[2:0]), .in_0(7'b1000001), .in_1(7'b0100000), .in_2(7'b1000001), .in_3(7'b0100000),
    .in_4(7'b0100000), .in_5(7'b0100000), .in_6(7'b1010011), .in_7(7'b1010011), .out(multiplexer_11_out));
  Multiplexer #(.Selector_Bits(3), .Bits(7)) multiplexer_12 (
    .sel(or_1_out), .in_0(7'b0100000), .in_1(7'b1000001), .in_2(7'b1001010), .in_3(multiplexer_11_out),
    .in_4(multiplexer_2_out), .in_5(multiplexer_5_out), .in_6(7'b0100000), .in_7(7'b0100000),
    .out(multiplexer_12_out));
  Multiplexer #(.Selector_Bits(3), .Bits(7)) multiplexer_13 (
    .sel(ALUControl[2:0]), .in_0(7'b1001110), .in_1(7'b1001111), .in_2(7'b1000100), .in_3(7'b0100000),
    .in_4(7'b0100000), .in_5(7'b0100000), .in_6(7'b1010101), .in_7(7'b1001100), .out(multiplexer_13_out));
  ROM #(.AddrBits(7), .Bits(16)) ASCII_4 (.A(multiplexer_12_out), .sel(1'b1), .D(D4));
  Multiplexer #(.Selector_Bits(3), .Bits(7)) multiplexer_14 (
    .sel(ALUControl[2:0]), .in_0(7'b1000100), .in_1(7'b1010010), .in_2(7'b1000100), .in_3(7'b0100000),
    .in_4(7'b0100000), .in_5(7'b0100000), .in_6(7'b1000010), .in_7(7'b1010100), .out(multiplexer_14_out));
  Multiplexer #(.Selector_Bits(3), .Bits(7)) multiplexer_15 (
    .sel(or_1_out), .in_0(7'b0100000), .in_1(7'b1001100), .in_2(7'b1000001), .in_3(multiplexer_13_out),
    .in_4(multiplexer_3_out), .in_5(multiplexer_8_out), .in_6(7'b1010011), .in_7(7'b1001100),
    .out(multiplexer_15_out));
  ROM #(.AddrBits(7), .Bits(16)) ASCII_5 (.A(multiplexer_15_out), .sel(1'b1), .D(D5));
  Multiplexer #(.Selector_Bits(3), .Bits(7)) multiplexer_16 (
    .sel(or_1_out), .in_0(7'b0100000), .in_1(7'b1010010), .in_2(7'b1001100), .in_3(multiplexer_14_out),
    .in_4(multiplexer_6_out), .in_5(multiplexer_9_out), .in_6(7'b1010111), .in_7(7'b1010111),
    .out(multiplexer_16_out));
  ROM #(.AddrBits(7), .Bits(16)) ASCII_6 (.A(multiplexer_16_out), .sel(1'b1), .D(D6));

  assign P1 = 1'b0;
  assign P2 = 1'b0;
  assign P3 = 1'b0;
  assign P4 = 1'b0;
  assign P5 = 1'b0;
  assign P6 = 1'b0;

  // Notes on the sheet:
  //   0000011
  //   0100011
  //   1100011
  //   0010011
  //   0110011
  //   1101111
  //   1100111
  //   contents of ASCII (hex, n*v repeats v):
  //   90ff,c,377,33f,38c,3bb,3fb,f,3ff,3bf,3cf,4a3f,f3,483f,3f3,1c3
  //   ,17*0,4800,4*0,2d79,4*0,4b00,0,300,0,0,90ff,c,377,33f,38c,3bb
  //   ,3fb,f,3ff,3bf,0,0,3000,0,8400,0,0,3cf,4a3f,f3,483f,3f3,1c3,2fb
  //   ,3cc,4833,7c,31c0,f0,14cc,24cc,ff,3c7,20ff,23c7,3bb,4803,fc,90c0
  //   ,a0cc,b400,5400,9033,0,0,0,a000
  //   contents of ASCII_2 (hex, n*v repeats v):
  //   90ff,c,377,33f,38c,3bb,3fb,f,3ff,3bf,3cf,4a3f,f3,483f,3f3,1c3
  //   ,17*0,4800,4*0,2d79,4*0,4b00,0,300,0,0,90ff,c,377,33f,38c,3bb
  //   ,3fb,f,3ff,3bf,0,0,3000,0,8400,0,0,3cf,4a3f,f3,483f,3f3,1c3,2fb
  //   ,3cc,4833,7c,31c0,f0,14cc,24cc,ff,3c7,20ff,23c7,3bb,4803,fc,90c0
  //   ,a0cc,b400,5400,9033,0,0,0,a000
  //   contents of ASCII_3 (hex, n*v repeats v):
  //   90ff,c,377,33f,38c,3bb,3fb,f,3ff,3bf,3cf,4a3f,f3,483f,3f3,1c3
  //   ,17*0,4800,4*0,2d79,4*0,4b00,0,300,0,0,90ff,c,377,33f,38c,3bb
  //   ,3fb,f,3ff,3bf,0,0,3000,0,8400,0,0,3cf,4a3f,f3,483f,3f3,1c3,2fb
  //   ,3cc,4833,7c,31c0,f0,14cc,24cc,ff,3c7,20ff,23c7,3bb,4803,fc,90c0
  //   ,a0cc,b400,5400,9033,0,0,0,a000
  //   contents of ASCII_4 (hex, n*v repeats v):
  //   90ff,c,377,33f,38c,3bb,3fb,f,3ff,3bf,3cf,4a3f,f3,483f,3f3,1c3
  //   ,17*0,4800,4*0,2d79,4*0,4b00,0,300,0,0,90ff,c,377,33f,38c,3bb
  //   ,3fb,f,3ff,3bf,0,0,3000,0,8400,0,0,3cf,4a3f,f3,483f,3f3,1c3,2fb
  //   ,3cc,4833,7c,31c0,f0,14cc,24cc,ff,3c7,20ff,23c7,3bb,4803,fc,90c0
  //   ,a0cc,b400,5400,9033,0,0,0,a000
  //   contents of ASCII_5 (hex, n*v repeats v):
  //   90ff,c,377,33f,38c,3bb,3fb,f,3ff,3bf,3cf,4a3f,f3,483f,3f3,1c3
  //   ,17*0,4800,4*0,2d79,4*0,4b00,0,300,0,0,90ff,c,377,33f,38c,3bb
  //   ,3fb,f,3ff,3bf,0,0,3000,0,8400,0,0,3cf,4a3f,f3,483f,3f3,1c3,2fb
  //   ,3cc,4833,7c,31c0,f0,14cc,24cc,ff,3c7,20ff,23c7,3bb,4803,fc,90c0
  //   ,a0cc,b400,5400,9033,0,0,0,a000
  //   contents of ASCII_6 (hex, n*v repeats v):
  //   90ff,c,377,33f,38c,3bb,3fb,f,3ff,3bf,3cf,4a3f,f3,483f,3f3,1c3
  //   ,17*0,4800,4*0,2d79,4*0,4b00,0,300,0,0,90ff,c,377,33f,38c,3bb
  //   ,3fb,f,3ff,3bf,0,0,3000,0,8400,0,0,3cf,4a3f,f3,483f,3f3,1c3,2fb
  //   ,3cc,4833,7c,31c0,f0,14cc,24cc,ff,3c7,20ff,23c7,3bb,4803,fc,90c0
  //   ,a0cc,b400,5400,9033,0,0,0,a000
endmodule
